# Fritzing sketch Hydra_cartpcb (saved by Fritzing 0.9.3b)
circuit board: 2.47472cm x 1.90025cm
breadboards: 1

parts:
  Pad1 = Pad [width=3.3999999999999999 height=8.4000000000000004 connect=north]
  Pad10 = Pad [width=3.3999999999999999 height=8.4000000000000004 connect=north]
  Pad11 = Pad [width=3.3999999999999999 height=8.4000000000000004 connect=north]
  Pad12 = Pad [width=3.3999999999999999 height=8.4000000000000004 connect=north]
  Pad13 = Pad [width=3.2000000000000002 height=4.5 connect=center]
  Pad14 = Pad [width=3.2000000000000002 height=4.5 connect=center]
  Pad15 = Pad [width=3.2000000000000002 height=4.5 connect=center]
  Pad16 = Pad [width=3.2000000000000002 height=4.5 connect=center]

nets:
  N1: Pad1.pad, Pad13.pad
  N2: Pad10.pad, Pad14.pad
  N3: Pad11.pad, Pad15.pad
  N4: Pad12.pad, Pad16.pad
